// Logisim project luc_1.circ as structural Verilog: 4 circuits, main circuit main
module main (
);

  wire nand_1_out, nand_2_out, nand_3_out, nand_4_out, nand_5_out, nand_6_out, nor_1_out, nor_2_out,
       nor_3_out, nor_4_out, nor_5_out, nor_6_out, undriven, undriven_2, undriven_3, undriven_4, undriven_5,
       undriven_6, undriven_7, undriven_8, undriven_9, undriven_10;

  nand nand_1 (nand_1_out, undriven, undriven);
  nor nor_1 (nor_1_out, undriven_2, undriven_2);
  nand nand_2 (nand_2_out, undriven_3, undriven_4);
  nor nor_2 (nor_2_out, undriven_5, undriven_5);
  nor nor_3 (nor_3_out, undriven_6, undriven_6);
  nand nand_3 (nand_3_out, nand_2_out, nand_2_out);
  nor nor_4 (nor_4_out, nor_2_out, nor_3_out);
  nand nand_4 (nand_4_out, undriven_7, undriven_7);
  nand nand_5 (nand_5_out, undriven_8, undriven_8);
  nor nor_5 (nor_5_out, undriven_9, undriven_10);
  nand nand_6 (nand_6_out, nand_4_out, nand_5_out);
  nor nor_6 (nor_6_out, nor_5_out, nor_5_out);

  // Notes on the sheet:
  //   NOT
  //   AND
  //   OR
endmodule

module SUMATOR (
  input  a0,
  input  a1,
  input  c
);

  wire nand_1_out, nand_2_out, nand_3_out, nand_4_out, nand_5_out, nand_6_out, nand_7_out, nand_8_out,
       nand_9_out, nand_10_out, nand_11_out, nand_12_out;

  nand nand_1 (nand_1_out, a0, a0);
  nand nand_2 (nand_2_out, a1, a1);
  nand nand_3 (nand_3_out, c, c);
  nand nand_4 (nand_4_out, nand_1_out, nand_2_out, c);
  nand nand_5 (nand_5_out, nand_1_out, a1, nand_3_out);
  nand nand_6 (nand_6_out, a0, a1, c);
  nand nand_7 (nand_7_out, a0, nand_2_out, nand_3_out);
  nand nand_8 (nand_8_out, a1, c);
  nand nand_9 (nand_9_out, a0, a1);
  nand nand_10 (nand_10_out, a0, c);
  nand nand_11 (nand_11_out, nand_10_out, nand_9_out, nand_8_out);
  nand nand_12 (nand_12_out, nand_7_out, nand_6_out, nand_5_out, nand_4_out);
  LED led_1 (.in(nand_11_out));
  LED led_2 (.in(nand_12_out));

  // Notes on the sheet:
  //   Sumator jednobitowy na NAND
  //   c
  //   y
endmodule

module KOMPARATOR (
  input  a1,
  input  in_2,
  input  in_3,
  input  in_4,
  input  a1_2,
  input  in_6,
  input  in_7,
  input  in_8,
  input  a1_3,
  input  in_10,
  input  in_11,
  input  in_12,
  input  a1_4,
  input  in_14,
  input  in_15,
  input  in_16,
  input  a1_5,
  input  in_18,
  input  in_19,
  input  in_20
);

  wire and_1_out, and_2_out, and_3_out, and_4_out, and_5_out, nand_1_out, nand_2_out, nand_3_out, nand_4_out,
       nand_5_out, nand_6_out, nand_7_out, nand_8_out, nand_9_out, nand_10_out, nand_11_out, nand_12_out,
       nand_13_out, nand_14_out, nand_15_out, nand_16_out, nand_17_out, nand_18_out, nand_19_out,
       nand_20_out, nand_21_out, nor_1_out, nor_2_out, nor_3_out, nor_4_out, nor_5_out, nor_6_out, nor_7_out,
       nor_8_out, nor_9_out, nor_10_out, nor_11_out, nor_12_out, nor_13_out, nor_14_out, nor_15_out,
       nor_16_out, nor_17_out, nor_18_out, not_1_out, not_2_out, not_3_out, not_4_out, not_5_out, not_6_out,
       not_7_out, not_8_out, not_9_out, not_10_out, not_11_out, not_12_out, not_13_out, or_1_out;

  not not_1 (not_1_out, in_4);
  not not_2 (not_2_out, in_3);
  not not_3 (not_3_out, in_4);
  not not_4 (not_4_out, in_3);
  not not_5 (not_5_out, in_3);
  and and_1 (and_1_out, not_1_out, not_2_out);
  and and_2 (and_2_out, in_2, a1);
  and and_3 (and_3_out, not_3_out, in_3, a1);
  and and_4 (and_4_out, in_4, not_4_out, a1);
  and and_5 (and_5_out, in_4, not_5_out, in_2);
  nand nand_1 (nand_1_out, in_20, in_20);
  nand nand_2 (nand_2_out, in_19, in_19);
  nand nand_3 (nand_3_out, in_20, in_20);
  nand nand_4 (nand_4_out, in_19, in_19);
  nand nand_5 (nand_5_out, in_19, in_19);
  nand nand_6 (nand_6_out, nand_1_out, nand_2_out);
  nand nand_7 (nand_7_out, in_18, a1_5);
  nand nand_8 (nand_8_out, nand_3_out, in_19, a1_5);
  nand nand_9 (nand_9_out, in_20, nand_4_out, a1_5);
  nand nand_10 (nand_10_out, in_20, nand_5_out, in_18);
  nand nand_11 (nand_11_out, nand_6_out, nand_7_out, nand_8_out, nand_9_out, nand_10_out);
  or or_1 (or_1_out, and_1_out, and_2_out, and_3_out, and_4_out, and_5_out);
  LED led_1 (.in(nand_11_out));
  LED led_2 (.in(or_1_out));
  nor nor_1 (nor_1_out, in_14, in_14);
  nor nor_2 (nor_2_out, a1_4, a1_4);
  nor nor_3 (nor_3_out, in_15, in_15);
  nor nor_4 (nor_4_out, a1_4, a1_4);
  nor nor_5 (nor_5_out, in_16, in_16);
  nor nor_6 (nor_6_out, a1_4, a1_4);
  nor nor_7 (nor_7_out, in_16, in_16);
  nor nor_8 (nor_8_out, in_14, in_14);
  nor nor_9 (nor_9_out, in_16, in_15);
  nor nor_10 (nor_10_out, nor_1_out, nor_2_out);
  nor nor_11 (nor_11_out, in_16, nor_3_out, nor_4_out);
  nor nor_12 (nor_12_out, nor_5_out, in_15, nor_6_out);
  nor nor_13 (nor_13_out, nor_7_out, in_15, nor_8_out);
  nor nor_14 (nor_14_out, nor_9_out, nor_10_out, nor_11_out, nor_12_out, nor_13_out);
  nor nor_15 (nor_15_out, nor_14_out, nor_14_out);
  LED led_3 (.in(nor_15_out));
  nor nor_16 (nor_16_out, in_8, in_7);
  not not_6 (not_6_out, in_8);
  not not_7 (not_7_out, in_7);
  not not_8 (not_8_out, in_7);
  not not_9 (not_9_out, nor_16_out);
  nand nand_12 (nand_12_out, in_6, a1_2);
  nand nand_13 (nand_13_out, not_6_out, in_7, a1_2);
  nand nand_14 (nand_14_out, in_8, not_7_out, a1_2);
  nand nand_15 (nand_15_out, in_8, not_8_out, in_6);
  nand nand_16 (nand_16_out, not_9_out, nand_12_out, nand_13_out, nand_14_out, nand_15_out);
  LED led_4 (.in(nand_16_out));
  not not_10 (not_10_out, in_12);
  not not_11 (not_11_out, in_11);
  not not_12 (not_12_out, in_11);
  nor nor_17 (nor_17_out, in_12, in_11);
  nand nand_17 (nand_17_out, in_10, a1_3);
  nand nand_18 (nand_18_out, not_10_out, in_11, a1_3);
  nand nand_19 (nand_19_out, in_12, not_11_out, a1_3);
  nand nand_20 (nand_20_out, in_12, not_12_out, in_10);
  nand nand_21 (nand_21_out, nand_17_out, nand_18_out, nand_19_out, nand_20_out);
  nor nor_18 (nor_18_out, nor_17_out, nand_21_out);
  not not_13 (not_13_out, nor_18_out);
  LED led_5 (.in(not_13_out));

  // Notes on the sheet:
  //   a0
  //   b1
  //   a0
  //   b0
  //   b1
  //   b0
  //   a0
  //   b1
  //   b0
  //   a0
  //   b1
  //   b0
  //   a0
  //   b1
  //   b0
endmodule

module MULTIPLEKSER (
  input  in_1,
  input  a1,
  input  in_3,
  input  in_4,
  input  a1_2,
  input  in_6,
  input  in_7,
  input  a1_3,
  input  in_9
);

  wire and_1_out, and_2_out, nand_1_out, nand_2_out, nand_3_out, nor_1_out, nor_2_out, nor_3_out, nor_4_out,
       nor_5_out, nor_6_out, nor_7_out, not_1_out, not_2_out, or_1_out;

  not not_1 (not_1_out, in_3);
  nor nor_1 (nor_1_out, in_6, in_6);
  nor nor_2 (nor_2_out, a1_2, a1_2);
  nor nor_3 (nor_3_out, in_4, in_4);
  and and_1 (and_1_out, in_3, a1);
  and and_2 (and_2_out, not_1_out, in_1);
  nor nor_4 (nor_4_out, nor_1_out, nor_2_out);
  nor nor_5 (nor_5_out, in_6, nor_3_out);
  or or_1 (or_1_out, and_1_out, and_2_out);
  nor nor_6 (nor_6_out, nor_4_out, nor_5_out);
  LED led_1 (.in(or_1_out));
  nor nor_7 (nor_7_out, nor_6_out, nor_6_out);
  LED led_2 (.in(nor_7_out));
  not not_2 (not_2_out, in_9);
  nand nand_1 (nand_1_out, in_9, a1_3);
  nand nand_2 (nand_2_out, not_2_out, in_7);
  nand nand_3 (nand_3_out, nand_1_out, nand_2_out);
  LED led_3 (.in(nand_3_out));

  // Notes on the sheet:
  //   a0
  //   a0
  //   S
  //   S
  //   stan S 0 przeniosi a0 stan S 1 przenosi a1
  //   stan S 0 przeniosi a0 stan S 1 przenosi a1
  //   a0
  //   S
  //   stan S 0 przeniosi a0 stan S 1 przenosi a1
endmodule
