// Logisim project lab10.circ as structural Verilog: 1 circuit, main circuit main
module main (
  input  p,
  input  z,
  output y,
  output s1,
  output s2
);

  wire c_out, nand_1_out, nand_2_out, nand_3_out, nand_5_out, not_1_out, not_2_out, q1_qn, q2_q, q2_qn,
       xor_1_out, xor_2_out;

  not not_1 (not_1_out, p);
  not not_2 (not_2_out, z);
  Button c (.out(c_out));
  xor xor_1 (xor_1_out, z, q2_q);
  nand nand_1 (nand_1_out, xor_1_out, not_1_out, q1_qn);
  nand nand_2 (nand_2_out, q2_qn, p, not_2_out);
  nand nand_3 (nand_3_out, z, p, q1_qn);
  nand nand_4 (s2, nand_1_out, nand_2_out);
  not not_3 (s1, nand_3_out);
  D_Flip_Flop q1 (.D(s1), .clk(c_out), .Qn(q1_qn));  // open: Q, preset, reset
  D_Flip_Flop q2 (.D(s2), .clk(c_out), .Q(q2_q), .Qn(q2_qn));  // open: preset, reset
  xor xor_2 (xor_2_out, p, q2_q);
  nand nand_5 (nand_5_out, q1_qn, xor_2_out);
  not not_4 (y, nand_5_out);
endmodule
