// Logisim project lab02.circ as structural Verilog
module rejestrrowszer (
  input  E,
  input  Q1,
  input  Q2,
  input  Q3,
  input  Q4,
  output out_6
);

  wire C_out, d_ff_1_q, d_ff_2_q, d_ff_3_q, nand_1_out, nand_2_out, nand_3_out, nand_4_out, nand_5_out,
       nand_6_out, nand_7_out, nand_8_out, nand_9_out, nand_10_out, nand_11_out, nand_12_out, nand_13_out,
       nand_14_out, nand_15_out, nand_16_out, not_1_out, not_2_out, not_3_out, not_4_out;

  nand nand_1 (nand_1_out, E, Q1);
  Button C (.out(C_out));
  nand nand_2 (nand_2_out, Q1, 1'b0);
  nand nand_3 (nand_3_out, nand_1_out, nand_2_out, nand_4_out);
  not not_1 (not_1_out, E);
  nand nand_4 (nand_4_out, not_1_out, 1'b0);
  D_Flip_Flop d_ff_1 (.D(nand_3_out), .clk(C_out), .Q(d_ff_1_q));  // open: Qn, preset, reset
  nand nand_5 (nand_5_out, E, Q2);
  nand nand_6 (nand_6_out, Q2, d_ff_1_q);
  nand nand_7 (nand_7_out, nand_5_out, nand_6_out, nand_8_out);
  not not_2 (not_2_out, E);
  nand nand_8 (nand_8_out, not_2_out, d_ff_1_q);
  D_Flip_Flop d_ff_2 (.D(nand_7_out), .clk(C_out), .Q(d_ff_2_q));  // open: Qn, preset, reset
  nand nand_9 (nand_9_out, E, Q3);
  not not_3 (not_3_out, E);
  nand nand_10 (nand_10_out, Q3, d_ff_2_q);
  nand nand_11 (nand_11_out, not_3_out, d_ff_2_q);
  D_Flip_Flop d_ff_3 (.D(nand_12_out), .clk(C_out), .Q(d_ff_3_q));  // open: Qn, preset, reset
  nand nand_12 (nand_12_out, nand_9_out, nand_10_out, nand_11_out);
  nand nand_13 (nand_13_out, E, Q4);
  not not_4 (not_4_out, E);
  nand nand_14 (nand_14_out, Q4, d_ff_3_q);
  D_Flip_Flop d_ff_4 (.D(nand_15_out), .clk(C_out), .Q(out_6));  // open: Qn, preset, reset
  nand nand_15 (nand_15_out, nand_13_out, nand_14_out, nand_16_out);
  nand nand_16 (nand_16_out, not_4_out, d_ff_3_q);
endmodule

module licznikmod9wdolasynch (
  output q1,
  output q2,
  output q3,
  output q4
);

  wire button_1_out, C_out, d_ff_1_q, j_k_ff_1_qn, j_k_ff_2_qn, j_k_ff_3_q, j_k_ff_4_q, j_k_ff_5_qn,
       j_k_ff_6_q, j_k_ff_7_qn, nand_1_out, nor_1_out, nor_2_out;

  Button C (.out(C_out));
  J_K_Flip_Flop j_k_ff_1 (
    .J(1'b1), .K(1'b1), .clk(C_out), .Q(q4), .Qn(j_k_ff_1_qn), .reset(nand_1_out));  // open: preset
  Button button_1 (.out(button_1_out));
  J_K_Flip_Flop j_k_ff_2 (.J(1'b1), .K(1'b1), .clk(q4), .Q(q3), .Qn(j_k_ff_2_qn), .reset(nand_1_out));  // open: preset
  J_K_Flip_Flop j_k_ff_3 (.J(1'b1), .K(1'b1), .clk(button_1_out), .Q(j_k_ff_3_q));  // open: Qn, preset, reset
  J_K_Flip_Flop j_k_ff_4 (.J(1'b1), .K(1'b1), .clk(j_k_ff_3_q), .Q(j_k_ff_4_q));  // open: Qn, preset, reset
  J_K_Flip_Flop j_k_ff_5 (.J(1'b1), .K(1'b1), .clk(q3), .Q(q2), .Qn(j_k_ff_5_qn), .reset(nand_1_out));  // open: preset
  J_K_Flip_Flop j_k_ff_6 (.J(1'b1), .K(1'b1), .clk(j_k_ff_4_q), .Q(j_k_ff_6_q));  // open: Qn, preset, reset
  J_K_Flip_Flop j_k_ff_7 (.J(1'b1), .K(1'b1), .clk(q2), .Q(q1), .Qn(j_k_ff_7_qn), .preset(nand_1_out));  // open: reset
  J_K_Flip_Flop j_k_ff_8 (.J(1'b1), .K(1'b1), .clk(j_k_ff_6_q));  // open: Q, Qn, preset, reset
  D_Flip_Flop d_ff_1 (.D(nor_1_out), .clk(C_out), .Q(d_ff_1_q));  // open: Qn, preset, reset
  nor nor_1 (nor_1_out, q4, q3, q2, q1);
  nor nor_2 (nor_2_out, j_k_ff_7_qn, j_k_ff_5_qn, j_k_ff_2_qn, j_k_ff_1_qn);
  nand nand_1 (nand_1_out, d_ff_1_q, nor_2_out);
endmodule

module liczniksymmod9d (
  output Q3,
  output Q2,
  output Q1,
  output Q0
);

  wire C_out, nand_1_out, nand_2_out, nor_1_out, not_1_out, not_2_out, R_out, xor_1_out, xor_2_out;

  D_Flip_Flop d_ff_1 (.D(not_1_out), .clk(C_out), .Q(Q3), .reset(R_out));  // open: Qn, preset
  nand nand_1 (nand_1_out, Q0, Q1, Q2);
  not not_1 (not_1_out, nand_1_out);
  Button C (.out(C_out));
  Button R (.out(R_out));
  nand nand_2 (nand_2_out, Q1, Q0);
  not not_2 (not_2_out, nand_2_out);
  D_Flip_Flop d_ff_2 (.D(xor_1_out), .clk(C_out), .Q(Q2), .reset(R_out));  // open: Qn, preset
  xor xor_1 (xor_1_out, not_2_out, Q2);
  D_Flip_Flop d_ff_3 (.D(xor_2_out), .clk(C_out), .Q(Q1), .reset(R_out));  // open: Qn, preset
  xor xor_2 (xor_2_out, Q0, Q1);
  D_Flip_Flop d_ff_4 (.D(nor_1_out), .clk(C_out), .Q(Q0), .reset(R_out));  // open: Qn, preset
  nor nor_1 (nor_1_out, Q0, Q3);
endmodule
