// Logisim project automat.circ as structural Verilog: 2 circuits, main circuit main
module main (
  input  z1,
  input  z0,
  output y
);

  wire c_out, j_k_ff_1_q, j_k_ff_1_qn, j_k_ff_2_q, j_k_ff_2_qn, j_k_ff_3_qn, nand_1_out, nand_2_out,
       nand_3_out, nand_4_out, nand_5_out, nand_6_out, nor_1_out, nor_2_out, not_1_out, not_2_out, not_3_out,
       r_out, xor_1_out;

  not not_1 (not_1_out, z1);
  not not_2 (not_2_out, z0);
  Button c (.out(c_out));
  Button r (.out(r_out));
  nand nand_1 (nand_1_out, not_1_out, not_2_out, j_k_ff_2_qn, j_k_ff_3_qn);
  nor nor_1 (nor_1_out, z1, z0, j_k_ff_2_qn, j_k_ff_3_qn);
  J_K_Flip_Flop j_k_ff_1 (
    .J(nor_1_out), .K(nand_1_out), .clk(c_out), .Q(j_k_ff_1_q), .Qn(j_k_ff_1_qn), .reset(r_out));  // open: preset
  xor xor_1 (xor_1_out, z1, z0);
  not not_3 (not_3_out, xor_1_out);
  nor nor_2 (nor_2_out, z1, z0, j_k_ff_1_q, j_k_ff_3_qn);
  J_K_Flip_Flop j_k_ff_2 (
    .J(nor_2_out), .K(nand_2_out), .clk(c_out), .Q(j_k_ff_2_q), .Qn(j_k_ff_2_qn), .reset(r_out));  // open: preset
  nand nand_2 (nand_2_out, not_3_out, j_k_ff_3_qn);
  nand nand_3 (nand_3_out, not_1_out, not_2_out, j_k_ff_1_q);
  nand nand_4 (nand_4_out, z1, z0, j_k_ff_2_q);
  nand nand_5 (nand_5_out, not_1_out, not_2_out, j_k_ff_2_qn);
  nand nand_6 (nand_6_out, nand_4_out, nand_5_out);
  J_K_Flip_Flop j_k_ff_3 (
    .J(nand_6_out), .K(nand_3_out), .clk(c_out), .Q(y), .Qn(j_k_ff_3_qn), .reset(r_out));  // open: preset

  // Notes on the sheet:
  //   1
  //   2
  //   3
  //   !1
  //   !2
  //   !3
endmodule

module millie (
  input  z1,
  input  z0,
  output Y
);

  wire c_out, j_k_ff_1_q, j_k_ff_1_qn, j_k_ff_2_q, j_k_ff_2_qn, j_k_ff_3_q, j_k_ff_3_qn, nand_1_out,
       nand_2_out, nand_3_out, nand_4_out, nand_5_out, nor_1_out, nor_2_out, not_1_out, not_2_out, not_3_out,
       R_out, xor_1_out;

  not not_1 (not_1_out, z1);
  not not_2 (not_2_out, z0);
  Button c (.out(c_out));
  Button R (.out(R_out));
  nor nor_1 (nor_1_out, z1, z0, j_k_ff_2_qn, j_k_ff_3_qn);
  J_K_Flip_Flop j_k_ff_1 (
    .J(nor_1_out), .K(1'b1), .clk(c_out), .Q(j_k_ff_1_q), .Qn(j_k_ff_1_qn), .reset(R_out));  // open: preset
  xor xor_1 (xor_1_out, z1, z0);
  nor nor_2 (nor_2_out, z1, z0, j_k_ff_1_q, j_k_ff_3_qn);
  J_K_Flip_Flop j_k_ff_2 (
    .J(nor_2_out), .K(nand_1_out), .clk(c_out), .Q(j_k_ff_2_q), .Qn(j_k_ff_2_qn), .reset(R_out));  // open: preset
  not not_3 (not_3_out, xor_1_out);
  nand nand_1 (nand_1_out, not_3_out, j_k_ff_3_qn);
  nand nand_2 (nand_2_out, z1, z0, j_k_ff_2_q);
  nand nand_3 (nand_3_out, nand_2_out, nand_4_out);
  nand nand_4 (nand_4_out, not_2_out, not_1_out, j_k_ff_2_qn, j_k_ff_1_qn);
  J_K_Flip_Flop j_k_ff_3 (
    .J(nand_3_out), .K(1'b1), .clk(c_out), .Q(j_k_ff_3_q), .Qn(j_k_ff_3_qn), .reset(R_out));  // open: preset
  nand nand_5 (nand_5_out, j_k_ff_1_q, not_2_out, not_1_out);
  D_Flip_Flop d_ff_1 (.D(nand_5_out), .clk(c_out), .Q(Y), .reset(R_out));  // open: Qn, preset

  // Notes on the sheet:
  //   1
  //   2
  //   3
  //   !1
  //   !2
  //   !3
endmodule
