// Logisim project lab5.circ as structural Verilog: 1 circuit, main circuit main
module main (
  input  z,
  output out_2
);

  wire c_out, j_k_ff_1_q, j_k_ff_1_qn, j_k_ff_2_q, j_k_ff_2_qn, j_k_ff_3_q, j_k_ff_3_qn, nand_1_out,
       nand_2_out, nand_3_out, nand_4_out, nor_1_out, not_1_out, r_out, xnor_1_out;

  not not_1 (not_1_out, z);
  Button c (.out(c_out));
  Button r (.out(r_out));
  nand nand_1 (nand_1_out, z, j_k_ff_3_q, j_k_ff_2_q);
  nand nand_2 (nand_2_out, j_k_ff_3_qn, not_1_out);
  J_K_Flip_Flop j_k_ff_1 (
    .J(nand_3_out), .K(1'b0), .clk(c_out), .Q(j_k_ff_1_q), .Qn(j_k_ff_1_qn), .reset(r_out));  // open: preset
  nand nand_3 (nand_3_out, nand_1_out, nand_2_out);
  J_K_Flip_Flop j_k_ff_2 (
    .J(j_k_ff_3_q), .K(1'b1), .clk(c_out), .Q(j_k_ff_2_q), .Qn(j_k_ff_2_qn), .reset(r_out));  // open: preset
  xnor xnor_1 (xnor_1_out, j_k_ff_2_q, z);
  nor nor_1 (nor_1_out, not_1_out, j_k_ff_1_q);
  J_K_Flip_Flop j_k_ff_3 (
    .J(nor_1_out), .K(xnor_1_out), .clk(c_out), .Q(j_k_ff_3_q), .Qn(j_k_ff_3_qn), .reset(r_out));  // open: preset
  nand nand_4 (nand_4_out, j_k_ff_2_q, j_k_ff_3_qn, j_k_ff_1_qn);
  not not_2 (out_2, nand_4_out);

  // Notes on the sheet:
  //   3
  //   2
  //   1
  //   z2(z1z2+z2z1)*z1
endmodule
