// Logisim project lab7.circ as structural Verilog: 2 circuits, main circuit zzadania
module zzadania (
  input  x1,
  input  x2,
  output y1,
  output y2
);

  wire m1_out, m2_out, m3_out, m4_out, m5_out, m6_out, m7_out, m8_out, m9_out, not_1_out, not_2_out,
       not_3_out, not_4_out;

  not not_1 (not_1_out, x1);
  not not_2 (not_2_out, m7_out);
  nor m1 (m1_out, m7_out, m8_out);
  nor m2 (m2_out, m7_out, not_1_out);
  nor m3 (m3_out, x1, m8_out);
  nor m4 (m4_out, not_1_out, not_2_out);
  nor m5 (m5_out, m1_out, m2_out);
  nor m6 (m6_out, m3_out, m4_out);
  not not_3 (not_3_out, m5_out);
  not not_4 (not_4_out, m6_out);
  nor m8 (m8_out, x2, not_4_out);
  nor m7 (m7_out, not_3_out, x2);
  nor m9 (m9_out, m7_out, m8_out);
  not not_5 (y1, m9_out);
  nor m10 (y2, m8_out, not_2_out);

  // Notes on the sheet:
  //   q1
  //   q2
endmodule

module aaaaa (
  input  z1,
  input  z2,
  output q1,
  output q2,
  output q3,
  output y1,
  output y2
);

  wire m1_out, n1_out, n2_out, n4_out, n5_out, n6_out, n8_out, n9_out, n10_out, not_1_out, not_2_out,
       not_3_out, not_4_out, not_5_out, not_6_out;

  not not_1 (not_1_out, z1);
  not not_2 (not_2_out, z2);
  nor m1 (m1_out, not_1_out, not_4_out);
  nand n1 (n1_out, not_1_out, not_2_out, q2, not_6_out);
  nand n2 (n2_out, not_2_out, q1, q2, not_6_out);
  not not_3 (not_3_out, m1_out);
  nand n4 (n4_out, not_4_out, q3, not_1_out, not_2_out);
  nand n5 (n5_out, q2, not_6_out, not_1_out, not_2_out);
  nand n6 (n6_out, not_2_out, not_4_out, q2);
  nand n8 (n8_out, q3, not_5_out, not_4_out, not_2_out);
  nand n9 (n9_out, not_4_out, q3, not_1_out, not_2_out);
  nand n10 (n10_out, not_4_out, not_5_out, z1);
  nand n3 (q1, n1_out, n2_out, not_3_out);
  not not_4 (not_4_out, q1);
  nand n7 (q2, n4_out, n5_out, n6_out);
  not not_5 (not_5_out, q2);
  nand n11 (q3, n8_out, n9_out, n10_out);
  not not_6 (not_6_out, q3);
  nor m2 (y1, not_5_out, q3);
  nor m3 (y2, q1, not_6_out);

  // Notes on the sheet:
  //   z1 !z1 !z2
  //   q1 !q1
  //   q2 !q2
  //   q3 !q3
  //   1
  //   q1
  //   !q1
  //   q2
  //   !q2
  //   q3
  //   !q3
endmodule
