// Logisim project lab08.circ as structural Verilog: 2 circuits, main circuit main
module main (
  input  read,
  input  dwa,
  input  jeden,
  input  zero,
  input  s,
  input  r,
  output odczyt
);

  wire and_1_out, and_2_out, and_3_out, and_4_out, and_5_out, and_6_out, b1_out, b2_out, b3_out, m1_out,
       m2_out, m3_out, m4_out, m5_out, n1_out, n2_out, not_1_out, not_2_out, not_3_out, not_4_out, not_5_out,
       not_6_out, s_r_ff_1_q, s_r_ff_2_q, s_r_ff_3_q, s_r_ff_3_qn, v1_out, v2_out, v3_out;

  and and_1 (and_1_out, s_r_ff_1_q, zero);
  and and_2 (and_2_out, s, s_r_ff_3_qn);
  nor m1 (m1_out, read, dwa);
  nor v3 (v3_out, and_1_out, and_2_out);
  nor m2 (m2_out, s_r_ff_2_q, r);
  nor m3 (m3_out, r, zero);
  not b1 (b1_out, jeden);
  not not_1 (not_1_out, v3_out);
  S_R_Flip_Flop s_r_ff_1 (.Q(s_r_ff_1_q), .reset(not_2_out), .preset(not_1_out));  // open: S, R, clk, Qn
  not not_2 (not_2_out, m2_out);
  nand n1 (n1_out, m1_out, b1_out);
  not b3 (b3_out, m3_out);
  not b2 (b2_out, m1_out);
  and and_3 (and_3_out, n1_out, s_r_ff_1_q);
  and and_4 (and_4_out, jeden, s_r_ff_2_q);
  nor v2 (v2_out, and_3_out, and_4_out);
  not not_3 (not_3_out, v2_out);
  S_R_Flip_Flop s_r_ff_2 (.Q(s_r_ff_2_q), .reset(not_4_out), .preset(not_3_out));  // open: S, R, clk, Qn
  not not_4 (not_4_out, m4_out);
  nor m4 (m4_out, b3_out, s_r_ff_3_q);
  and and_5 (and_5_out, b2_out, s_r_ff_2_q);
  and and_6 (and_6_out, dwa, s_r_ff_3_q);
  nor v1 (v1_out, and_5_out, and_6_out);
  nor m5 (m5_out, jeden, b3_out);
  S_R_Flip_Flop s_r_ff_3 (.Q(s_r_ff_3_q), .reset(not_6_out), .Qn(s_r_ff_3_qn), .preset(not_5_out));  // open: S, R, clk
  not not_5 (not_5_out, v1_out);
  not not_6 (not_6_out, m5_out);
  nand n2 (n2_out, read, s_r_ff_3_q);
  not b4 (odczyt, n2_out);

  // Notes on the sheet:
  //   0*1*2*
  //   1
  //   2
  //   5x 2nor
  //   2x 2nand
  //   4x not
  //   3x magiczny układ
  //   3
endmodule

module nftmcosiedzieje (
  input  read,
  input  w2,
  input  w1,
  input  w0,
  input  start,
  output wyjscie
);

  wire and_1_out, and_2_out, and_3_out, and_4_out, and_5_out, and_6_out, and_7_out, and_8_out, and_9_out,
       and_10_out, b1_out, b2_out, b3_out, m1_out, m3_out, n1_out, not_1_out, not_2_out, not_3_out,
       not_4_out, not_5_out, not_6_out, not_7_out, not_8_out, s_r_ff_1_q, s_r_ff_1_qn, s_r_ff_2_q,
       s_r_ff_2_qn, s_r_ff_3_q, s_r_ff_3_qn, v1_out, v2_out, v3_out, v4_out, v5_out;

  not not_1 (not_1_out, read);
  not not_2 (not_2_out, start);
  and and_1 (and_1_out, w1, not_2_out);
  and and_2 (and_2_out, not_2_out, w2);
  nor m3 (m3_out, w2, w0);
  nor m1 (m1_out, w1, w0);
  not not_3 (not_3_out, not_2_out);
  S_R_Flip_Flop s_r_ff_1 (.Q(s_r_ff_1_q), .reset(not_4_out), .Qn(s_r_ff_1_qn), .preset(not_3_out));  // open: S, R, clk
  not not_4 (not_4_out, v3_out);
  nor v3 (v3_out, and_1_out, and_2_out);
  and and_3 (and_3_out, m3_out, not_2_out);
  and and_4 (and_4_out, not_2_out, s_r_ff_3_qn);
  and and_5 (and_5_out, s_r_ff_1_q, w2);
  and and_6 (and_6_out, w2, s_r_ff_2_q);
  and and_7 (and_7_out, m1_out, not_2_out);
  and and_8 (and_8_out, not_2_out, s_r_ff_2_qn);
  nor v5 (v5_out, and_3_out, and_4_out);
  not b1 (b1_out, v5_out);
  nor v1 (v1_out, and_5_out, and_6_out);
  not not_5 (not_5_out, v1_out);
  S_R_Flip_Flop s_r_ff_2 (.Q(s_r_ff_2_q), .reset(not_6_out), .Qn(s_r_ff_2_qn), .preset(not_5_out));  // open: S, R, clk
  not not_6 (not_6_out, b2_out);
  nor v2 (v2_out, and_7_out, and_8_out);
  not b2 (b2_out, v2_out);
  and and_9 (and_9_out, s_r_ff_1_q, w1);
  nor v4 (v4_out, and_9_out, and_10_out);
  not not_7 (not_7_out, v4_out);
  S_R_Flip_Flop s_r_ff_3 (.Q(s_r_ff_3_q), .reset(not_8_out), .Qn(s_r_ff_3_qn), .preset(not_7_out));  // open: S, R, clk
  not not_8 (not_8_out, b1_out);
  and and_10 (and_10_out, w1, s_r_ff_3_q);
  nand n1 (n1_out, s_r_ff_2_qn, s_r_ff_1_qn, s_r_ff_3_qn);
  not b3 (b3_out, n1_out);
  nor m2 (wyjscie, not_1_out, b3_out);

  // Notes on the sheet:
  //   0*1*+0*2*
  //   1
  //   3
  //   2
endmodule
