// Logisim project lab09.circ as structural Verilog: 1 circuit, main circuit main
module main (
  input  z1,
  input  z2,
  output y
);

  wire c_out, nand_1_out, nand_2_out, nand_3_out, nand_4_out, nand_5_out, nand_6_out, nand_7_out, not_1_out,
       not_2_out, not_3_out, q1_q, q1_qn, q2_q, r_out;

  not not_1 (not_1_out, z2);
  Button c (.out(c_out));
  Button r (.out(r_out));
  nand nand_1 (nand_1_out, z1, not_1_out);
  nand nand_2 (nand_2_out, nand_1_out, nand_3_out);
  nand nand_3 (nand_3_out, not_1_out, q2_q);
  J_K_Flip_Flop q1 (.J(nand_2_out), .K(1'b0), .clk(c_out), .Q(q1_q), .Qn(q1_qn), .reset(r_out));  // open: preset
  not not_2 (not_2_out, z1);
  nand nand_4 (nand_4_out, z2, not_2_out);
  nand nand_5 (nand_5_out, not_2_out, q1_q);
  nand nand_6 (nand_6_out, z1, q1_qn);
  J_K_Flip_Flop q2 (.J(nand_7_out), .K(not_3_out), .clk(c_out), .Q(q2_q), .reset(r_out));  // open: Qn, preset
  nand nand_7 (nand_7_out, nand_4_out, nand_5_out);
  not not_3 (not_3_out, nand_6_out);
  nand nand_8 (y, q1_q, q2_q);
endmodule
