// Logisim project e.circ as structural Verilog: 1 circuit, main circuit main
module main (
);

  wire and_1_out, and_2_out, and_3_out, and_4_out, and_5_out, and_6_out, and_7_out, button_1_out, d_ff_1_q,
       d_ff_2_q, d_ff_2_qn, d_ff_3_q, d_ff_3_qn, d_ff_4_q, d_ff_4_qn, or_1_out, or_2_out, xnor_1_out;

  Button button_1 (.out(button_1_out));
  xnor xnor_1 (xnor_1_out, d_ff_1_q, d_ff_4_q);
  D_Flip_Flop d_ff_1 (.D(and_1_out), .clk(button_1_out), .Q(d_ff_1_q));  // open: Qn, preset, reset
  and and_1 (and_1_out, xnor_1_out, d_ff_2_qn, d_ff_3_qn);
  and and_2 (and_2_out, d_ff_4_qn, d_ff_1_q);
  and and_3 (and_3_out, d_ff_3_q, d_ff_2_q);
  and and_4 (and_4_out, d_ff_4_q, d_ff_2_q);
  D_Flip_Flop d_ff_2 (.D(or_1_out), .clk(button_1_out), .Q(d_ff_2_q), .Qn(d_ff_2_qn));  // open: preset, reset
  or or_1 (or_1_out, and_4_out, and_2_out, and_3_out);
  and and_5 (and_5_out, d_ff_4_q, d_ff_3_q);
  and and_6 (and_6_out, d_ff_4_qn, d_ff_3_qn, d_ff_2_q);
  and and_7 (and_7_out, d_ff_4_qn, d_ff_1_q);
  D_Flip_Flop d_ff_3 (.D(or_2_out), .clk(button_1_out), .Q(d_ff_3_q), .Qn(d_ff_3_qn));  // open: preset, reset
  or or_2 (or_2_out, and_7_out, and_5_out, and_6_out);
  D_Flip_Flop d_ff_4 (.D(d_ff_4_qn), .clk(button_1_out), .Q(d_ff_4_q), .Qn(d_ff_4_qn));  // open: preset, reset
endmodule
