// Logisim project lab1.circ as structural Verilog: 1 circuit, main circuit main
module main (
  input  w,
  input  x1,
  input  x,
  input  x2,
  input  y,
  input  x3,
  input  z,
  input  x4
);

  wire and_1_out, and_2_out, and_3_out, and_4_out, and_5_out, and_6_out, and_7_out, and_8_out, and_9_out,
       not_1_out, not_2_out, not_4_out, not_6_out, not_7_out, not_8_out, not_10_out, not_12_out, or_1_out,
       or_2_out, or_3_out, or_4_out, or_5_out, or_6_out, or_7_out, or_8_out, or_9_out, xor_1_out, xor_2_out;

  not not_1 (not_1_out, w);
  not not_2 (not_2_out, x);
  not not_3 (not_2_out, x);
  not not_4 (not_4_out, y);
  not not_5 (not_4_out, y);
  not not_6 (not_6_out, z);
  or or_1 (or_1_out, y, not_2_out);
  and and_1 (and_1_out, not_1_out, not_4_out, z);
  and and_2 (and_2_out, not_6_out, or_1_out, w);
  or or_2 (or_2_out, and_1_out, and_2_out);
  LED led_1 (.in(or_2_out));
  not not_7 (not_7_out, x1);
  not not_8 (not_8_out, x2);
  not not_9 (not_8_out, x2);
  not not_10 (not_10_out, x3);
  not not_11 (not_10_out, x3);
  not not_12 (not_12_out, x4);
  and and_3 (and_3_out, x1, not_8_out, not_10_out);
  or or_3 (or_3_out, x4, x3);
  and and_4 (and_4_out, not_7_out, x2, or_3_out);
  or or_4 (or_4_out, and_3_out, and_4_out);
  LED y1 (.in(or_4_out));
  and and_5 (and_5_out, not_10_out, not_12_out);
  or or_5 (or_5_out, x3, and_5_out);
  and and_6 (and_6_out, x2, or_5_out);
  or or_6 (or_6_out, x1, and_6_out);
  LED y2 (.in(or_6_out));
  xor xor_1 (xor_1_out, x2, x3);
  and and_7 (and_7_out, xor_1_out, not_7_out, x4);
  xor xor_2 (xor_2_out, x1, x3);
  and and_8 (and_8_out, not_8_out, xor_2_out);
  or or_7 (or_7_out, and_7_out, and_8_out);
  LED y3 (.in(or_7_out));
  or or_8 (or_8_out, x2, x3);
  and and_9 (and_9_out, x1, or_8_out);
  or or_9 (or_9_out, x4, and_9_out);
  LED y4 (.in(or_9_out));
endmodule
